// Logisim project practica04.circ as structural Verilog: 12 circuits, main circuit sumador1Bit
module sumador1Bit (
  input  A,
  input  B,
  input  Cin,
  output suma,
  output acarreo_o_Cout
);

  wire and_1_out, and_2_out, and_3_out, and_4_out, and_5_out, and_6_out, and_7_out, not_1_out, not_2_out,
       not_3_out, not_4_out, not_5_out, not_6_out;

  not not_1 (not_1_out, B);
  not not_2 (not_2_out, Cin);
  not not_3 (not_3_out, A);
  not not_4 (not_4_out, B);
  not not_5 (not_5_out, A);
  not not_6 (not_6_out, Cin);
  and and_1 (and_1_out, A, Cin);
  and and_2 (and_2_out, A, B);
  and and_3 (and_3_out, B, Cin);
  and and_4 (and_4_out, A, not_1_out, not_2_out);
  and and_5 (and_5_out, not_3_out, not_4_out, Cin);
  and and_6 (and_6_out, A, B, Cin);
  and and_7 (and_7_out, not_5_out, B, not_6_out);
  or or_1 (acarreo_o_Cout, and_1_out, and_2_out, and_3_out);
  or or_2 (suma, and_4_out, and_5_out, and_6_out, and_7_out);

  // Notes on the sheet:
  //   Sumador de 1 bit
  //   A
  //   Cin
  //   A
  //   B
  //   B
  //   Cin
  //   A
  //   NEG B
  //   NEG Cin
  //   NEG A
  //   NEG B
  //   Cin
  //   Cin
  //   NEG A
  //   B
  //   Cin
  //   A
  //   B
endmodule

module sumador8bits (
  input  [7:0] A,
  input  [7:0] in_2,
  input  Cin,
  output [7:0] out_4,
  output Cout
);

  wire sumador1bit_1_acarreo_o_cout, sumador1bit_2_acarreo_o_cout, sumador1bit_3_acarreo_o_cout,
       sumador1bit_4_acarreo_o_cout, sumador1bit_5_acarreo_o_cout, sumador1bit_6_acarreo_o_cout,
       sumador1bit_7_acarreo_o_cout;

  sumador1Bit sumador1bit_1 (
    .A(A[0]), .B(in_2[0]), .Cin(Cin), .suma(out_4[0]), .acarreo_o_Cout(sumador1bit_1_acarreo_o_cout));
  sumador1Bit sumador1bit_2 (
    .A(A[1]), .B(in_2[1]), .Cin(sumador1bit_1_acarreo_o_cout), .suma(out_4[1]),
    .acarreo_o_Cout(sumador1bit_2_acarreo_o_cout));
  sumador1Bit sumador1bit_3 (
    .A(A[2]), .B(in_2[2]), .Cin(sumador1bit_2_acarreo_o_cout), .suma(out_4[2]),
    .acarreo_o_Cout(sumador1bit_3_acarreo_o_cout));
  sumador1Bit sumador1bit_4 (
    .A(A[3]), .B(in_2[3]), .Cin(sumador1bit_3_acarreo_o_cout), .suma(out_4[3]),
    .acarreo_o_Cout(sumador1bit_4_acarreo_o_cout));
  sumador1Bit sumador1bit_5 (
    .A(A[4]), .B(in_2[4]), .Cin(sumador1bit_4_acarreo_o_cout), .suma(out_4[4]),
    .acarreo_o_Cout(sumador1bit_5_acarreo_o_cout));
  sumador1Bit sumador1bit_6 (
    .A(A[5]), .B(in_2[5]), .Cin(sumador1bit_5_acarreo_o_cout), .suma(out_4[5]),
    .acarreo_o_Cout(sumador1bit_6_acarreo_o_cout));
  sumador1Bit sumador1bit_7 (
    .A(A[6]), .B(in_2[6]), .Cin(sumador1bit_6_acarreo_o_cout), .suma(out_4[6]),
    .acarreo_o_Cout(sumador1bit_7_acarreo_o_cout));
  sumador1Bit sumador1bit_8 (
    .A(A[7]), .B(in_2[7]), .Cin(sumador1bit_7_acarreo_o_cout), .suma(out_4[7]), .acarreo_o_Cout(Cout));

  // Notes on the sheet:
  //   B
  //   SUMADOR DE 8 BITS
  //   sumador 1
  //   sumador 2
  //   sumador 3
  //   sumador 4
  //   sumador 5
  //   sumador 6
  //   sumador 7
  //   sumador 8
endmodule

// D
module restador (
  input  [7:0] in_1,
  input  [7:0] in_2,
  output [7:0] sum_de_8_bits
);

  wire [7:0] not_1_out, sumador8bits_1_out_4;

  assign not_1_out = ~in_2;  // NOT_Gate not_1, 8 bits wide
  sumador8bits sumador8bits_1 (.A(not_1_out), .in_2(8'h1), .Cin(1'b0), .out_4(sumador8bits_1_out_4));  // open: Cout
  sumador8bits sumador8bits_2 (.A(in_1), .in_2(sumador8bits_1_out_4), .Cin(1'b0), .out_4(sum_de_8_bits));  // open: Cout

  // Notes on the sheet:
  //   A
  //   B
  //   RESTADOR DE 8 BITS
  //   7 bits apagados
  //   1 bit encendido
  //   complemento a 1 de B
  //   sum de 8 bits
  //   Cin
  //   comp a 2 de B
  //   Cin
  //   A
  //   los 8 bits, i.e. nunca habra un 
  //   desbordamiento
  //   representamos el resultado en 8 bits
  //   ya que el resultado de la resta de dos
  //   numeros de 8 bits nunca superara los
endmodule

// S
module sumador (
  input  [7:0] in_1,
  input  [7:0] in_2,
  output [15:0] out_3
);

  sumador16bits sumador16bits_1 (
    .in_1({{8{1'b0}}, in_1}), .in_2({{8{1'b0}}, in_2}), .Cin(1'b0), .out_4(out_3));  // open: Cout

  // Notes on the sheet:
  //   A
  //   B
  //   8 bits nulos
  //   SUMADOR DE 8 BITS CON SALIDA DE 16 BITS
  //   A de 16 bits
  //   B en 16 bits
  //   Cin nulo
  //   sumador de 16 bits
  //   representamos el resultado en 16 bits
  //   ya que puede haber un desbordamiento
endmodule

module sumador16bits (
  input  [15:0] in_1,
  input  [15:0] in_2,
  input  Cin,
  output [15:0] out_4,
  output Cout
);

  wire sumador8bits_1_cout;

  sumador8bits sumador8bits_1 (
    .A(in_1[7:0]), .in_2(in_2[7:0]), .Cin(Cin), .out_4(out_4[7:0]), .Cout(sumador8bits_1_cout));
  sumador8bits sumador8bits_2 (
    .A(in_1[15:8]), .in_2(in_2[15:8]), .Cin(sumador8bits_1_cout), .out_4(out_4[15:8]), .Cout(Cout));

  // Notes on the sheet:
  //   SUMADOR DE 16 BITS
  //   8-15bits
  //   A
  //   0-7 bits
  //   8-15bits
  //   B
  //   0-7 bits
  //   0-7 bits de A
  //   0-7 bits de B
  //   8-15 bits de A
  //   8-15 bits de B
  //   sumador 8 bits
  //   Cout
  //   sumador 8 bits
  //   0-7 bits
  //   8-15bits
  //   salida de 16 bits
endmodule

module sumRest (
  input  [7:0] in_1,
  input  in_2,
  input  [7:0] in_3,
  output [15:0] resultado
);

  wire [7:0] restador_1_sum_de_8_bits;
  wire [15:0] sumador_1_out_3;

  sumador sumador_1 (.in_1(in_1), .in_2(in_3), .out_3(sumador_1_out_3));
  restador restador_1 (.in_1(in_1), .in_2(in_3), .sum_de_8_bits(restador_1_sum_de_8_bits));
  Multiplexer #(.width(16), .enable("false")) multiplexer_1 (
    .in0(sumador_1_out_3), .in1({{8{1'b0}}, restador_1_sum_de_8_bits}), .out(resultado), .sel(in_2));

  // Notes on the sheet:
  //   A
  //   B
  //   MULTIPLEXOR PARA LA SUMA Y LA RESTA
  //   resta
  //   completamos con 8 bits nulos
  //   para representarlo en 16 bits
  //   suma
  //   Multiplexor
  //   1 = haz resta
  //   0 = haz suma
endmodule

module restadorVisual (
  input  [7:0] in_1,
  input  [7:0] in_2,
  output [7:0] sum_de_8_bits,
  output [7:0] comp_a_1_de_B,
  output [7:0] comp_a_2_de_B,
  output [7:0] out_6
);

  assign comp_a_1_de_B = ~in_2;  // NOT_Gate not_1, 8 bits wide
  sumador8bits sumador8bits_1 (.A(comp_a_1_de_B), .in_2(8'h1), .Cin(1'b0), .out_4(comp_a_2_de_B));  // open: Cout
  sumador8bits sumador8bits_2 (.A(in_1), .in_2(comp_a_2_de_B), .Cin(1'b0), .out_4(sum_de_8_bits));  // open: Cout

  assign out_6 = 8'h1;

  // Notes on the sheet:
  //   A
  //   B
  //   7 bits apagados
  //   1 bit encendido
  //   RESTADOR DE 8 BITS CON SALIDAS VISUALES
  //   Cin
  //   numero 1 en 8 bits
  //   sum de 8 bits
  //   comp a 2 de B
  //   Cin
  //   A
  //   desbordamiento
  //   representamos el resultado en 8 bits
  //   ya que el resultado de la resta de dos
  //   numeros de 8 bits nunca superara los
  //   los 8 bits, i.e. nunca habra un 
endmodule

module igualdad (
  input  [7:0] in_1,
  input  [7:0] in_2,
  output out_3
);

  wire [7:0] and8bits_1_out_3, not_1_out, not_2_out, restador_1_sum_de_8_bits;

  restador restador_1 (.in_1(in_1), .in_2(in_2), .sum_de_8_bits(restador_1_sum_de_8_bits));
  assign not_1_out = ~restador_1_sum_de_8_bits;  // NOT_Gate not_1, 8 bits wide
  assign not_2_out = ~{8{1'b0}};  // NOT_Gate not_2, 8 bits wide
  and8bits and8bits_1 (.in_1(not_1_out), .in_2(not_2_out), .out_3(and8bits_1_out_3));
  and and_1 (out_3, and8bits_1_out_3[0], and8bits_1_out_3[1], and8bits_1_out_3[2], and8bits_1_out_3[3], and8bits_1_out_3[4], and8bits_1_out_3[5], and8bits_1_out_3[6], and8bits_1_out_3[7]);

  // Notes on the sheet:
  //   de manera que
  //   AND
  //   A
  //   B
  //   IGUALDAD DE DOS NUMEROS
  //   con el complemento a 1 de cero
  //   11111111
  //   11111111
  //   ------------------------
  //   1
  //   Si el resultado de restar A y B es igual a cero
  //   entonces solo basta sacar el complemento a 1
  //   del resultado y pasarlo al circuito and de 8 bits
  //   comp a 1 de cero
  //   cero representado en 8 bits
  //   00000000
  //   resultado de A-B = 0
  //   con A=B
  //   complemento a 1 de A-B
  //   11111111
  //   complemento a 1 de cero
  //   and8bits
endmodule

module and1bit (
  input  A,
  input  B,
  output out_3
);

  and and_1 (out_3, A, B);

  // Notes on the sheet:
  //   AND DE 1 BIT
endmodule

module and8bits (
  input  [7:0] in_1,
  input  [7:0] in_2,
  output [7:0] out_3
);

  and1bit and1bit_1 (.A(in_1[0]), .B(in_2[0]), .out_3(out_3[0]));
  and1bit and1bit_2 (.A(in_1[1]), .B(in_2[1]), .out_3(out_3[1]));
  and1bit and1bit_3 (.A(in_1[2]), .B(in_2[2]), .out_3(out_3[2]));
  and1bit and1bit_4 (.A(in_1[3]), .B(in_2[3]), .out_3(out_3[3]));
  and1bit and1bit_5 (.A(in_1[4]), .B(in_2[4]), .out_3(out_3[4]));
  and1bit and1bit_6 (.A(in_1[5]), .B(in_2[5]), .out_3(out_3[5]));
  and1bit and1bit_7 (.A(in_1[6]), .B(in_1[6]), .out_3(out_3[6]));
  and1bit and1bit_8 (.A(in_2[7]), .B(in_1[7]), .out_3(out_3[7]));

  assign in_2[6] = in_1[6];

  // Notes on the sheet:
  //   A
  //   B
  //   and1
  //   and2
  //   and3
  //   and4
  //   and5
  //   and6
  //   and7
  //   and8
endmodule

module or1bit (
  input  A,
  input  B,
  output out_3
);

  or or_1 (out_3, A, B);
endmodule

module or8bits (
  input  [7:0] in_1,
  input  [7:0] in_2,
  output [7:0] out_3
);

  or1bit or1bit_1 (.A(in_1[0]), .B(in_2[0]), .out_3(out_3[0]));
  or1bit or1bit_2 (.A(in_1[1]), .B(in_2[1]), .out_3(out_3[1]));
  or1bit or1bit_3 (.A(in_1[2]), .B(in_2[2]), .out_3(out_3[2]));
  or1bit or1bit_4 (.A(in_1[3]), .B(in_2[3]), .out_3(out_3[3]));
  or1bit or1bit_5 (.A(in_1[4]), .B(in_2[4]), .out_3(out_3[4]));
  or1bit or1bit_6 (.A(in_1[5]), .B(in_2[5]), .out_3(out_3[5]));
  or1bit or1bit_7 (.A(in_1[6]), .B(in_1[6]), .out_3(out_3[6]));
  or1bit or1bit_8 (.A(in_2[7]), .B(in_1[7]), .out_3(out_3[7]));

  assign in_2[6] = in_1[6];

  // Notes on the sheet:
  //   OR DE 8 BITS
  //   A
  //   B
  //   or1
  //   or2
  //   or3
  //   or4
  //   or5
  //   or6
  //   or7
  //   or8
endmodule
